# Fritzing sketch Alltogether (saved by Fritzing 0.9.2b)
breadboards: 1

parts:
  LCD1 = LCD screen
  Parte1 = Arduino Uno (Rev3)
  R1 = Resistor [tolerance=±5% resistance=220 package=THT]
  R2 = Rotary Potentiometer (Small) [maximum_resistance=10kΩ package=THT]  # not connected
  LED1 = RGB LED (com. cathode, rgb) [package="5 mm [THT]"]
  R3 = Resistor [tolerance=±5% resistance=220 package=THT]
  R4 = Resistor [tolerance=±5% resistance=220 package=THT]
  R5 = Resistor [tolerance=±5% resistance=220 package=THT]
  S1 = Pushbutton [package="[THT]"]
  R6 = Resistor [tolerance=±5% resistance=220 package=THT]
  J1 = Piezo Speaker

nets (from the breadboard view):
  VSS: LCD1.VSS, Parte1.GND, LED1.green_anode, R6.Pin_1, J1.pin1
  VDD: LCD1.VDD, Parte1.5V, R1.Pin_0
  N1: LCD1.RS, Parte1.D12/MISO
  N2: LCD1.E, Parte1.D11_PWM/MOSI
  N3: LCD1.DB4, Parte1.D5_PWM
  N4: LCD1.DB5, Parte1.D4
  N5: LCD1.DB6, Parte1.D3_PWM
  N6: LCD1.DB7, Parte1.D2
  N7: LCD1.LED+, R1.Pin_1
  N8: Parte1.D8, R5.Pin_1
  N9: Parte1.D9_PWM, R4.Pin_1
  N10: Parte1.D10_PWM/SS, R3.Pin_1
  N11: Parte1.D6_PWM, J1.pin2
  N12: Parte1.D7, S1.Pin_3, S1.Pin_4
  N13: LED1.red_anode, R3.Pin_0
  N14: LED1.common_cathode, R4.Pin_0
  N15: LED1.blue_anode, R5.Pin_0
  N16: S1.Pin_1, S1.Pin_2, R6.Pin_0
